# Fritzing sketch Red LED 8x8 max7219 (saved by Fritzing 0.9.10b)
breadboards: 1

parts:
  V1 = DC Power [voltage=5]
  Mod1 = Amica NodeMCU DEVKIT 1.0
  Part1 = Matrix LED de 8x8 basada en MAX7219

nets:
  N1: V1.V-, Mod1.pin2, Mod1.pin_9, Part1.GND
  N2: Mod1.pin1, Mod1.pin_10, Part1.VCC
  N3: Mod1.pin5, Part1.CLK
  N4: Mod1.pin6, Part1.DIN
  N5: Mod1.pin8, Part1.CS
